# Fritzing sketch HV_synthesized (saved by Fritzing 0.9.3b)
breadboards: 1

parts:
  Main_Battery = Battery Holders [package=battery-aa]
  U1 = RELAY [package=relay-g5q]
  F1 = FUSE [package=fuse_5mm]
  F2 = FUSE [package=fuse_5mm]
  BMS_Fuse = FUSE [package=fuse_5mm]
  Controller = IC, DIP package, 4 pins [chip_label=IC]
  Motor = IC, DIP package, 4 pins [chip_label=Motor]
  Ignition_Switch = SWITCH-MOMENTARY-2 [package=tactile-pth-12mm]
  Precharge_Switch = SWITCH-MOMENTARY-2 [package=tactile-pth-12mm]
  R1 = Resistor [tolerance=±5% resistance=200k package=THT]
  Buck_Converter = IC, DIP package, 4 pins [chip_label=IC]
  Emergency_Shutoff = SWITCH-MOMENTARY-2 [package=tactile-pth-12mm]
  Orion_BMS_2 = IC, SIP package, 26 pins [chip_label=IC]
  BMS_Power_Switch = SWITCH-MOMENTARY-2 [package=tactile-pth-12mm]
  AUX_Battery = SIP - 2 pins [chip_label=IC package="SIP (Single Inline) [THT]"]
  U2 = RELAY [package=relay-g5q]
  AC/DC_Power_Supply = IC, SIP package, 3 pins [chip_label=IC]
  Charge_Controller = IC, DIP package, 4 pins [chip_label=IC]

nets:
  N1: Main_Battery.-, U1.NO, Precharge_Switch.1, Buck_Converter.pin2
  GND: Main_Battery.+, U1.COIL1, Controller.pin1, Motor.pin2, Buck_Converter.pin4, Orion_BMS_2.pin12, AUX_Battery.pin1, U2.COIL2, AC/DC_Power_Supply.pin1, Charge_Controller.pin3
  N2: U1.COIL2, Emergency_Shutoff.2
  N3: U1.MAIN, F1.1, R1.Pin_1
  N4: F1.2, Controller.pin4, Motor.pin3
  N5: F2.1, AUX_Battery.pin2
  N6: BMS_Fuse.1, Ignition_Switch.1, Buck_Converter.pin3
  N7: BMS_Fuse.2, BMS_Power_Switch.1
  N8: Controller.pin2, Motor.pin1
  N9: Ignition_Switch.2, Emergency_Shutoff.1
  N10: Precharge_Switch.2, R1.Pin_0
  N11: Orion_BMS_2.pin1, BMS_Power_Switch.2
  N12: Orion_BMS_2.pin6, AC/DC_Power_Supply.pin2
  N13: Orion_BMS_2.pin8, U2.COIL1
  N14: U2.MAIN, Charge_Controller.pin2
  N15: U2.NC, Charge_Controller.pin1
  N16: AC/DC_Power_Supply.pin3, Charge_Controller.pin4

notes:
  Low voltage will can be integrated by using voltage from Buck Converter output and the BMS, AUX as backup
  Next:
  - Put in Horn Relay system
  - BMS Fault Switch at ground
  - Integrate Low voltage
  - Investigate BMS pins
  - Source Components
  Uncertainties:
  - Charge Controller
  - Buck Converter
  - Precharge Circuit
  - Location of Emergency Shutoff
  Vedrik: (2/27)
  - Precharge Circuit/Ignition Relay
  ~ Precharge Switch can be a relay/contactor controlled by BMS
  ~ Need to calculate resistor Value
  - Relays
  ~ Use EMS Relay for ignition switch (Simple and effective)
  ~ SSR for emergency shutoff, Charge Controller relay (Faster transient response)
  - Charger Controller Circuit
  ~ BMS will check power, enable charging and allow Charge Controller to charge battery
  ~ Wire the circuit in a way that will make an easy SCC transition later on
  - Grounding
  ~ Check the grounding (Common, Floating, Isolated)
  - Switches
  ~ Emergency Shutoff Location, We can have two: Manual in the beginning (NC), and BMS controlled switch between the Motor/Motor Controller and battery ground (NC)
