# Fritzing sketch Pegboard (saved by Fritzing 0.9.3b)
breadboards: 3
stripboards: 4

parts:
  Part1 = Arduino Uno (Rev3)
  Raspberry_Pi_1 = Raspberry Pi 3 [part_number=RPI-3-V1.2]  # not connected
  RELAY1 = CAR RELAY [part_number=NVF4-2 package=THT]
  RELAY2 = CAR RELAY [part_number=NVF4-2 package=THT]
  J2 = female pin header, 2 pins [form="♀ (female)"]  # not connected
  J3 = female pin header, 2 pins [form="♀ (female)"]  # not connected
  S1 = Round Pushbutton
  LED1 = SMD RGB LED (WS2812) [package=5050]  # not connected
  LED3 = SMD RGB LED (WS2812) [package=5050]  # not connected
  LED4 = SMD RGB LED (WS2812) [package=5050]  # not connected
  LED5 = SMD RGB LED (WS2812) [package=5050]  # not connected
  LED6 = SMD RGB LED (WS2812) [package=5050]  # not connected
  LED7 = SMD RGB LED (WS2812) [package=5050]  # not connected
  LED8 = SMD RGB LED (WS2812) [package=5050]  # not connected
  LED9 = SMD RGB LED (WS2812) [package=5050]  # not connected
  LED10 = SMD RGB LED (WS2812) [package=5050]  # not connected
  LED11 = SMD RGB LED (WS2812) [package=5050]  # not connected
  LED13 = SMD RGB LED (WS2812) [package=5050]  # not connected
  S3 = Round Pushbutton
  S4 = Round Pushbutton
  M1 = Niren can bus module [package=THT]
  LED14 = smd LED [color="Yellow (595nm)" package="0603 [SMD]"]
  LED15 = smd LED [color="Yellow (595nm)" package="0603 [SMD]"]
  OMRON1 = OMRON PCB Power Relay – G5LE [part_number="G5LE-1\n" package=THT]
  LED12 = SMD RGB LED (WS2812) [package=5050]
  R2 = Resistor [tolerance=±5% resistance=116k package=THT]
  R1 = Resistor [tolerance=±5% resistance=116k package=THT]
  R4 = Resistor [tolerance=±5% resistance=22k package=THT]
  R3 = Resistor [tolerance=±5% resistance=48k package=THT]
  R5 = Resistor [tolerance=±5% resistance=48k package=THT]
  R6 = Resistor [tolerance=±5% resistance=22k package=THT]
  R7 = Resistor [tolerance=±5% resistance=22k package=THT]
  R8 = Resistor [tolerance=±5% resistance=48k package=THT]
  R9 = Resistor [tolerance=±5% resistance=22k package=THT]
  R10 = Resistor [tolerance=±5% resistance=48k package=THT]
  F2 = FUSE [package=fuse_5mm]
  F3 = FUSE [package=fuse_5mm]
  F4 = FUSE [package=fuse_5mm]
  F5 = FUSE [package=fuse_5mm]
  F6 = FUSE [package=fuse_5mm]
  F7 = FUSE [package=fuse_5mm]
  J4 = female pin header, 2 pins [form="♀ (female)"]
  LED16 = SMD RGB LED (WS2812) [package=5050]
  LED17 = SMD RGB LED (WS2812) [package=5050]  # not connected
  LED18 = SMD RGB LED (WS2812) [package=5050]  # not connected
  LED19 = SMD RGB LED (WS2812) [package=5050]  # not connected
  LED20 = SMD RGB LED (WS2812) [package=5050]  # not connected
  LED21 = SMD RGB LED (WS2812) [package=5050]  # not connected
  S2 = Round Pushbutton
  DPDT_Relay1 = DPDT Relay [chip_label=Relay package="DIP (Dual Inline) [THT]"]
  DPDT_Relay2 = DPDT Relay [chip_label=Relay package="DIP (Dual Inline) [THT]"]

nets:
  N1: Part1.D10_PWM/SS, M1.pin3
  N2: Part1.D11_PWM/MOSI, M1.pin5
  N3: Part1.D12/MISO, M1.pin4
  N4: Part1.D13/SCK, M1.pin6
  N5: Part1.D2, R7.Pin_0, R8.Pin_0
  N6: Part1.D3_PWM, R5.Pin_0, R6.Pin_0
  N7: Part1.D7, R4.Pin_0, R3.Pin_0
  N8: Part1.GND, RELAY2.85, LED16.DOut, DPDT_Relay2.pin1
  N9: RELAY1.85, LED12.DIn
  N10: RELAY1.30, RELAY2.30, S1.leg0, S3.leg0, S4.leg0, F7.1, S2.leg0
  N11: RELAY1.86, DPDT_Relay2.pin5
  N12: RELAY1.87, LED15.anode, R1.Pin_0
  N13: RELAY2.86, DPDT_Relay2.pin4
  N14: RELAY2.87, LED14.anode, R2.Pin_0
  N15: S1.leg1, R3.Pin_1
  N16: S3.leg1, DPDT_Relay2.pin8
  N17: S4.leg1, R5.Pin_1
  N18: M1.pin11, M1.pin13
  N19: LED14.cathode, R2.Pin_1
  N20: LED15.cathode, R1.Pin_1
  N21: OMRON1.A, LED16.DIn
  N22: R4.Pin_1, R6.Pin_1, R7.Pin_1, R9.Pin_1
  N23: R8.Pin_1, S2.leg1
  N24: R9.Pin_0, R10.Pin_0
  N25: F2.2, F3.2, F4.2, F5.2, F6.2, F7.2, J4.pin1
  N26: J4.pin2, DPDT_Relay1.pin2

notes:
  TB 1
  1
  2
  3
  4
  PiCAN Hat
  +12V
  GND
  CAN_L
  CAN_H
  R2
  R1
  a
  b
  SB-R
  SB-L
  SB-HZ
  SB-HL
  LCU 2
  LCU 1
  Flasher 1
  Flasher 2
  R3
  R6
  R8
  R10
  R7
  R9
  R5
  R4
  LED-L
  LED-R
  LED-HL
  5
  6
  Primary Fuse Box
  LED-BR
  Left: -
  Right: +
  Top: L
  Bottom: I
  Middle: H
  TB 2
  W1
  W2
  W3
  W4
  W5
  W6
  W7
  W8
  W10
  W11
  W12
  W13
  W14
  W15
  W16
  W17
  W18
  W19
  W20
  W21
  W22
  W23
  W24
  W25
  W26
  W27
  W28
  W29
  W30
  W90
  W91
  W95
  W94
  W92
  W93
  W96

custom parts:
  Niren can bus module: Niren can bus module availabe on ebay and others. No pcb view as no mechanical drawng and it wouldn't mount anyway.
  DPDT Relay: DIP DPDT Relay (Double Pole Double Throw)
