# Fritzing sketch Telemetry_Draft1 (saved by Fritzing 0.9.4)
breadboards: 1

parts:
  Raspi = Raspberry Pi 3 [part_number=RPI-3-V1.2]
  TCU_&_MCU = Arduino Uno (Rev3)
  M2 = Niren can bus module [package=THT]
  R1 = Resistor [tolerance=±5% resistance=120 package="2010 [SMD]"]
  Lights_Controller = Arduino Uno (Rev3)
  M3 = Niren can bus module [package=THT]
  R2 = Resistor [tolerance=±5% resistance=120 package="2010 [SMD]"]
  Pican2_Hat = Raspberry Pi Zero
  J1 = Screw terminal - 2 pins [package=THT]

nets (from the breadboard view):
  3V3: Raspi.3v3, Raspi.GPIO2, Raspi.GPIO4, Raspi.GPIO17, Raspi.GPIO22, Raspi.3V3, Raspi.GPIO9, Raspi.ID_SD, Raspi.GPIO19, Raspi.GPIO12, Raspi.GPIO24, Raspi.GPIO23, Raspi.GPIO18, Raspi.GPIO14, Raspi.5V, Pican2_Hat.pin_6, Pican2_Hat.pin_9, Pican2_Hat.pin_14, Pican2_Hat.pin_20, Pican2_Hat.pin_23, Pican2_Hat.pin_24, Pican2_Hat.pin_25, Pican2_Hat.pin_26, Pican2_Hat.pin_29, Pican2_Hat.pin_30, Pican2_Hat.pin_33, Pican2_Hat.pin_34, Pican2_Hat.pin_37, Pican2_Hat.pin_38, Pican2_Hat.pin_39, Pican2_Hat.pin_40
  N1: Raspi.GPIO3, Raspi.GND, Raspi.GPIO27, Raspi.GPIO26, Raspi.GPIO15, Pican2_Hat.pin_2, Pican2_Hat.pin_4, Pican2_Hat.pin_7, Pican2_Hat.pin_11, Pican2_Hat.pin_16, Pican2_Hat.pin_21, Pican2_Hat.pin_27, Pican2_Hat.pin_28, Pican2_Hat.pin_31, Pican2_Hat.pin_32, Pican2_Hat.pin_35, Pican2_Hat.pin_36
  N2: Raspi.GPIO10, Pican2_Hat.pin_22
  N3: Raspi.GPIO11, Pican2_Hat.pin_18
  N4: Raspi.GPIO5, Pican2_Hat.pin_12
  N5: Raspi.GPIO6, Pican2_Hat.pin_10
  N6: Raspi.GPIO13, Pican2_Hat.pin_8
  N7: Raspi.GPIO21, Raspi.GPIO8, Pican2_Hat.pin_1, Pican2_Hat.pin_17
  N8: Raspi.GPIO20, Pican2_Hat.pin_3
  N9: Raspi.GPIO16, Pican2_Hat.pin_5
  N10: Raspi.ID_SC, Pican2_Hat.pin_13
  N11: Raspi.GPIO7, Pican2_Hat.pin_15
  N12: Raspi.GPIO25, Pican2_Hat.pin_19
  N13: TCU_&_MCU.D10_PWM/SS, M2.pin3
  N14: TCU_&_MCU.D11_PWM/MOSI, M2.pin5
  N15: TCU_&_MCU.D12/MISO, M2.pin4
  N16: TCU_&_MCU.D13/SCK, M2.pin6
  N17: TCU_&_MCU.GND, M2.pin2, M3.pin2
  N18: TCU_&_MCU.5V, M2.pin1
  N19: M2.pin10, M2.pin12
  N20: M2.pin11, M2.pin13
  N21: R1.Pin_0, R1.Pin_1, R2.Pin_0, R2.Pin_1, J1.pin1, J1.pin2
  N22: Lights_Controller.D10_PWM/SS, M3.pin3
  N23: Lights_Controller.D11_PWM/MOSI, M3.pin5
  N24: Lights_Controller.D12/MISO, M3.pin4
  N25: Lights_Controller.D13/SCK, M3.pin6
  N26: Lights_Controller.5V, M3.pin1
  N27: M3.pin10, M3.pin12
  N28: M3.pin11, M3.pin13

notes:
  CAN Hi - top
  CAN Lo - bottom
  Pican2
  CAN Hi
  Can Lo
  Connect Raspi to
  HDMI OR DSI DISPLAY

custom parts:
  Niren can bus module: Niren can bus module availabe on ebay and others. No pcb view as no mechanical drawng and it wouldn't mount anyway.
  Raspberry Pi Zero: The Raspberry Pi Zero is half the size of a Model A+, with twice the utility. A tiny Raspberry Pi that’s affordable enough for any project! · 1Ghz, Single-core CPU · 512MB RAM · Mini HDMI and USB On-The-Go ports · Micro USB power · HAT-compatible 40-pin header. Jan 2018: In this version schematic has been changed so the pins match the GPIO connector. I.e. the left hand pins are all the pins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
