# Fritzing sketch highvoltage_pegboard (saved by Fritzing 0.9.3b)

parts:
  DPDT_Relay1 = DPDT Relay [chip_label=Relay package="DIP (Dual Inline) [THT]"]
  Main_Battery = Battery block 9V
  DPDT_Relay2 = DPDT Relay [chip_label=Relay package="DIP (Dual Inline) [THT]"]
  DPDT_Relay3 = DPDT Relay [chip_label=Relay package="DIP (Dual Inline) [THT]"]
  Horn = SWITCH-MOMENTARY-2 [package=tactile-pth-12mm]
  Ignition = SWITCH-MOMENTARY-2 [package=tactile-pth-12mm]
  External_Shutoff = SWITCH-MOMENTARY-2 [package=tactile-pth-12mm]
  BMS_Fault = SWITCH-MOMENTARY-2 [package=tactile-pth-12mm]
  BMS_Power = SWITCH-MOMENTARY-2 [package=tactile-pth-12mm]
  Ignition_Relay = RELAY [package=relay-jzc]
  Relay_0 = RELAY [package=relay-jzc]
  Aux_FB_5 = FUSE [package=fuse_5mm]
  Aux_FB_4 = FUSE [package=fuse_5mm]
  Horn_Relay = CAR RELAY [part_number=NVF4-2 package=THT]
  Terminal_Block_2 = COMPUTER-PERIPHERAL-POWER [package=computer-peripheral-power]
  TB2+ = Header 1 [package=snap-male]
  TB2- = Header 1 [package=snap-male]
  Horn_2 = Microphone
  R1 = Resistor [tolerance=±5% resistance=220 package="0603 [SMD]"]
  Green_LED = LEDs [package=led10mm]
  White_LED1 = LEDs [package=led10mm]
  Orange_LED = LEDs [package=led10mm]
  Relay_6 = RELAY [package=relay-t9a]
  Relay_7 = RELAY [package=relay-t9a]
  DPDT_Relay4 = DPDT Relay [chip_label=Relay package="DIP (Dual Inline) [THT]"]
  Ignition_LED2 = LEDs [package=led10mm]
  Ignition_LED3 = LEDs [package=led10mm]
  Battery_- = Header 1 [package=snap-male]
  Solar_Panel_+ = Header 1 [package=snap-male]  # not connected
  Solar_Panel_- = Header 1 [package=snap-male]  # not connected
  Battery_+ = Header 1 [package=snap-male]
  Load_- = Header 1 [package=snap-male]  # not connected
  Load_+ = Header 1 [package=snap-male]
  Relay_8 = RELAY [package=relay-t9a]
  Secondary_Aux_Battery = Battery block 9V
  MCU_Power = Header 1 [package=snap-male]

nets:
  N1: DPDT_Relay1.pin1, BMS_Power.2
  N2: DPDT_Relay1.pin2, DPDT_Relay1.pin7, DPDT_Relay2.pin2, DPDT_Relay3.pin1, Horn.1, External_Shutoff.1, BMS_Power.1, Relay_0.COIL1, Terminal_Block_2.5V, DPDT_Relay4.pin2
  N3: DPDT_Relay1.pin3, White_LED1.A
  N4: DPDT_Relay1.pin5, Green_LED.A
  N5: DPDT_Relay1.pin6, Orange_LED.A
  GND: DPDT_Relay1.pin8, DPDT_Relay3.pin8, BMS_Fault.2, Ignition_Relay.COIL2, Horn_2.pin1, Green_LED.C, White_LED1.C, Orange_LED.C, Relay_6.COIL2, Relay_7.COIL2, DPDT_Relay4.pin8, Ignition_LED2.C, Ignition_LED3.C, Relay_8.COIL2
  N6: Main_Battery.-, Ignition.1, Ignition_Relay.MAIN
  N7: Main_Battery.+, TB2-.1
  N8: DPDT_Relay2.pin1, External_Shutoff.2
  N9: DPDT_Relay2.pin4, DPDT_Relay3.pin2
  N10: DPDT_Relay2.pin6, DPDT_Relay3.pin7
  N11: DPDT_Relay2.pin8, BMS_Fault.1
  N12: DPDT_Relay3.pin3, DPDT_Relay4.pin1
  N13: DPDT_Relay3.pin5, Relay_0.MAIN
  N14: Horn.2, Horn_Relay.85
  N15: Ignition.2, Ignition_Relay.COIL1
  N16: Ignition_Relay.NO, Aux_FB_5.1, Aux_FB_4.1
  N17: Relay_0.COIL2, Horn_Relay.86, Terminal_Block_2.NC
  N18: Relay_0.NO, Relay_6.COIL1, Relay_7.COIL1, Relay_8.COIL1
  N19: Aux_FB_5.2, TB2+.1
  N20: Aux_FB_4.2, Horn_Relay.30
  N21: Horn_Relay.87, R1.Pin_0
  N22: Horn_2.pin2, R1.Pin_1
  N23: Relay_6.MAIN, Relay_7.MAIN, Load_+.1
  N24: Relay_6.NO, MCU_Power.1
  N25: DPDT_Relay4.pin3, Ignition_LED2.A, Ignition_LED3.A
  N26: Battery_-.1, Relay_8.MAIN
  N27: Battery_+.1, Relay_8.NC, Secondary_Aux_Battery.+
  N28: Relay_8.NO, Secondary_Aux_Battery.-

notes:
  Task:
  - Synthesize Relays
  - Integrate ACTUAL components(battery/bms/Throttle/Charge Controller/Motor)
  - Isolate Components (their own ground)
  External Shutoff switch reversed
  During testing, we grounded Relay 2 Coil- instead of using BMS fault switch
  Relay 0 starts High Voltage system (MCU/Battery/Charge Controller)
  System Check: Relay 1-4
  High Voltage: Relay 5-8
  TB2 + = TB2-1 &TB2-2
  TB2 - = TB2-3 &TB2-4

custom parts:
  DPDT Relay: DIP DPDT Relay (Double Pole Double Throw)
